// Logisim project imm_gen.circ as structural Verilog: 2 circuits, main circuit imm_gen
module imm_gen (
  input  [31:0] inst,
  input  [2:0] ImmSel,
  output [31:0] imm
);

  IformatImm iformatimm_1 (.inst(inst));  // open: imm
  Multiplexer #(.enable("false"), .select(3), .width(32)) multiplexer_1 (.sel(ImmSel));  // open: in0, in1, in2, in3, in4, in5, in6, in7, out

  // Notes on the sheet:
  //   INPUTS to your circuit
  //   DON'T CHANGE THE LOCATIONS OF THE INPUTS AND OUTPUTS!
  //   OUTPUT from your circuit
endmodule

module IformatImm (
  input  [31:0] inst,
  output [31:0] imm
);

  assign imm = {{20{inst[31]}}, inst[31:20]};  // Bit_Extender bit_extender_1
endmodule
